// Logisim project circuito.circ as structural Verilog: 4 circuits, main circuit main
module main (
  input  A0,
  input  A1,
  input  A2,
  input  A3
);

  wire a_1_out_5, b_1_out_5, c_1_out_5;

  _7_Segment_Display u_7_segment_display_1 (.a(a_1_out_5), .b(b_1_out_5), .c(c_1_out_5));  // open: g, f, e, d, dp
  A a_1 (.A0(A0), .A1(A1), .A2(A2), .A3(A3), .out_5(a_1_out_5));
  C c_1 (.A0(A0), .A1(A1), .A2(A2), .A3(A3), .out_5(c_1_out_5));
  B b_1 (.A0(A0), .A1(A1), .A2(A2), .A3(A3), .out_5(b_1_out_5));
endmodule

module A (
  input  A0,
  input  A1,
  input  A2,
  input  A3,
  output out_5
);

  wire and_1_out, and_2_out, nor_1_out, not_1_out, or_1_out, or_2_out;

  or or_1 (or_1_out, A0, A1);
  not not_1 (not_1_out, A0);
  or or_2 (or_2_out, not_1_out, A1);
  nor nor_1 (nor_1_out, A0, A1, A3);
  and and_1 (and_1_out, or_1_out, A3);
  and and_2 (and_2_out, A2, or_2_out);
  or or_3 (out_5, nor_1_out, and_1_out, and_2_out);
endmodule

module B (
  input  A0,
  input  A1,
  input  A2,
  input  A3,
  output out_5
);

  wire and_1_out, and_2_out, and_3_out, nor_1_out, not_1_out, not_2_out, not_3_out, or_1_out;

  not not_1 (not_1_out, A2);
  not not_2 (not_2_out, A1);
  nor nor_1 (nor_1_out, A0, A2);
  and and_1 (and_1_out, nor_1_out, A1);
  or or_1 (or_1_out, A1, not_1_out);
  and and_2 (and_2_out, or_1_out, not_3_out);
  not not_3 (not_3_out, A3);
  and and_3 (and_3_out, A3, not_2_out, A0);
  or or_2 (out_5, and_1_out, and_2_out, and_3_out);
endmodule

module C (
  input  A0,
  input  A1,
  input  A2,
  input  A3,
  output out_5
);

  wire and_1_out, and_2_out, and_3_out, nor_1_out, not_1_out, not_2_out;

  nor nor_1 (nor_1_out, A0, A1);
  not not_1 (not_1_out, A3);
  and and_1 (and_1_out, nor_1_out, A3);
  not not_2 (not_2_out, A2);
  and and_2 (and_2_out, A2, not_1_out);
  and and_3 (and_3_out, A0, not_2_out);
  or or_1 (out_5, and_1_out, and_3_out, and_2_out);
endmodule
